# Fritzing sketch Robo5 (saved by Fritzing 0.9.2b)
breadboards: 2

parts:
  Part1 = Arduino Uno (Rev3)
  DHT1 = DHT11 Humitidy and Temperature Sensor
  Part2 = Bluetooth HC-06

nets:
  N1: Part1.D0/RX, Part2.TXD
  N2: Part1.D1/TX, Part2.RXD
  N3: Part1.D2, DHT1.DATA
  5V: Part1.5V, DHT1.VDD, Part2.VCC
  GND: Part1.GND, DHT1.GND, Part2.GND

custom parts:
  DHT11 Humitidy and Temperature Sensor: DHT11 Humidity and Temperature Sensor
