# Fritzing sketch robo1 (saved by Fritzing 0.9.2b)
breadboards: 1

parts:
  LED1 = LED - 5mm [color="Red (633nm)" package="5 mm [THT]"]
  Part1 = Arduino Uno (Rev3)
  R1 = Resistor [tolerance=±5% resistance=220 package=THT]
  Part2 = Bluetooth HC-06

nets (from the breadboard view):
  GND: LED1.cathode, Part1.GND, Part2.GND
  N1: LED1.anode, R1.Pin_1
  N2: Part1.D13/SCK, R1.Pin_0
  N3: Part1.D0/RX, Part2.TXD
  N4: Part1.D1/TX, Part2.RXD
  5V: Part1.5V, Part2.VCC
