# Fritzing sketch robo3 (saved by Fritzing 0.9.2b)
breadboards: 1

parts:
  Part1 = Arduino Uno (Rev3)
  J1 = Basic Servo
  Part2 = Bluetooth HC-06

nets:
  N1: Part1.D9_PWM, J1.pulse
  N2: Part1.D11_PWM/MOSI, Part2.RXD
  VCC: Part1.5V, J1.vcc, Part2.VCC
  GND: Part1.GND, J1.gnd, Part2.GND
