# Fritzing sketch robo4 (saved by Fritzing 0.9.2b)
breadboards: 1

parts:
  Part1 = Arduino Uno (Rev3)
  Part2 = Bluetooth HC-06
  IC1 = L293D [package=THT]
  M1 = DC Motor
  VCC1 = Battery block 9V
  M2 = DC Motor

nets:
  N1: Part1.D10_PWM/SS, Part2.TXD
  N2: Part1.D11_PWM/MOSI, Part2.RXD
  N3: Part1.D3_PWM, IC1.In_1
  N4: Part1.D4, IC1.In_4
  N5: Part1.D5_PWM, IC1.In_2
  N6: Part1.D6_PWM, IC1.In_3
  5V: Part1.5V, Part2.VCC, IC1.Enable_1, IC1.Enable_2, IC1.+V
  N7: Part1.VIN, VCC1.+
  N8: Part2.GND, IC1.0V, VCC1.-
  N9: IC1.Out_1_(_Controlled_by_Enable_1_), M2.pin_2
  N10: IC1.Out_2_(_Controlled_by_Enable_1_), M2.pin_1
  N11: IC1.Out_3_(_Controlled_by_Enable_2_), M1.pin_2
  N12: IC1.Out_4_(_Controlled_by_Enable_2_), M1.pin_1
